# Fritzing sketch square waves generator (saved by Fritzing 0.9.2b)
breadboards: 1

parts:
  R1 = Resistor [tolerance=±5% resistance=10k package=THT]
  R2 = Resistor [tolerance=±5% resistance=10k package=THT]
  R3 = Resistor [tolerance=±5% resistance=220 package=THT]
  R4 = Resistor [tolerance=±5% resistance=1 package=THT]
  R5 = Resistor [tolerance=±5% resistance=1 package=THT]
  Part1 = Arduino Uno (Rev3)
  IC1 = DIP - 8 pins [part_number=LM741 package="DIP (Dual Inline) [THT]"]
  C2 = Electrolytic Capacitor [capacitance=22µF package="100 mil [THT, electrolytic]"]  # not connected

nets:
  N1: R1.Pin_0, IC1.pin2
  N2: R1.Pin_1, R3.Pin_0, Part1.A1, IC1.pin6
  N3: R2.Pin_0, R3.Pin_1, IC1.pin3
  N4: R2.Pin_1, R4.Pin_1, R5.Pin_0, Part1.A0
  N5: R4.Pin_0, Part1.5V, IC1.pin7
  N6: R5.Pin_1, Part1.GND, IC1.pin4

custom parts:
  DIP - 8 pins: A DIP stand-in part for whatever IC you want. With 8 pins on a 300 mil dual inline package (DIP) footprint.
